# Fritzing sketch NodeMcu32s_LoRa_GPS_OLED (saved by Fritzing 0.9.3b)
circuit board: 12cm x 8cm
breadboards: 1

parts:
  Squix1 = OLED 0.96" 128x64 I2C SSD1306
  Bauteil1 = u-blox NEO-6M GPS Breakout
  U5 = ESP32S-HiLetgo [part_number=ESP32S-HiLetgo]
  RFM9x_LoRa_Radio_868_MHz = Adafruit RFM9x LoRa Radio
  Antenna_868_MHz = Antenna

nets:
  VCC: Squix1.VCC, Bauteil1.VCC, U5.3.3, RFM9x_LoRa_Radio_868_MHz.VIN
  GND: Squix1.GND, Bauteil1.GND, U5.GND, RFM9x_LoRa_Radio_868_MHz.GND
  N1: Squix1.SCL, U5.GPIO22
  N2: Squix1.SCA, U5.GPIO21
  N3: Bauteil1.RXD, U5.GPIO26
  N4: Bauteil1.TXD, U5.GPIO25
  N5: U5.GPIO27, RFM9x_LoRa_Radio_868_MHz.DIO1
  N6: U5.GPIO15, RFM9x_LoRa_Radio_868_MHz.DIO0
  N7: U5.GPIO4, RFM9x_LoRa_Radio_868_MHz.RST
  N8: U5.GPIO5, RFM9x_LoRa_Radio_868_MHz.CS
  N9: U5.GPIO18, RFM9x_LoRa_Radio_868_MHz.SCK
  N10: U5.GPIO19, RFM9x_LoRa_Radio_868_MHz.MISO
  N11: U5.GPIO23, RFM9x_LoRa_Radio_868_MHz.MOSI
  N12: RFM9x_LoRa_Radio_868_MHz.ANTENNA, Antenna_868_MHz.antenna_lead

custom parts:
  ESP32S-HiLetgo: HiLetgo ESP-WROOM-32 ESP32 ESP-32S Development Board 2.4GHz Dual-Mode WiFi + Bluetooth Dual Cores Microcontroller The ESP32 integrated with Antenna switches, RF Balun, power amplifiers, low-noise amplifiers, filters, and management modules, and the entire solution occupies the least area of PCB. 2.4 GHz Wi-Fi plus Bluetooth dual-mode chip, with TSMC Ultra-low power consumption 40nm technology,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
  Adafruit RFM9x LoRa Radio: Sending data over long distances is like magic, and now you can be a magician with this range of powerful and easy-to-use radio modules. Sure, sometimes you want to talk to a computer (a good time to use WiFi) or perhaps communicate with a Phone (choose Bluetooth Low Energy!) but what if you want to send data very far? Most WiFi, Bluetooth, Zigbee and other wireless chipsets use 2.4GHz, which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
