# Fritzing sketch NodeMcu_LoRa_GPS_OLED (saved by Fritzing 0.9.2b)
circuit board: 12cm x 8cm
breadboards: 1

parts:
  part = OLED 0.96" 128x64 I2C SSD1306
  RFM9x_LoRa = Adafruit RFM9x LoRa Radio
  Bauteil1 = u-blox NEO-6M GPS Breakout
  U4 = NodeMCU V2.0

nets (from the pcb view):
  VCC: part.VCC, RFM9x_LoRa.VIN, Bauteil1.VCC, U4.3V3
  GND: part.GND, RFM9x_LoRa.GND
  N1: part.SCL, U4.D1
  N2: part.SCA, U4.D2
  N3: RFM9x_LoRa.DIO0, U4.S3
  N4: RFM9x_LoRa.SCK, U4.D5
  N5: RFM9x_LoRa.MISO, U4.D6
  N6: RFM9x_LoRa.MOSI, U4.D7
  N7: RFM9x_LoRa.CS, U4.D8
  N8: Bauteil1.GND, U4.D4
  N9: Bauteil1.TXD, U4.D3
  N10: Bauteil1.RXD, U4.GND#6, U4.GND#13, U4.GND#16, U4.GND#33

custom parts:
  Adafruit RFM9x LoRa Radio: Sending data over long distances is like magic, and now you can be a magician with this range of powerful and easy-to-use radio modules. Sure, sometimes you want to talk to a computer (a good time to use WiFi) or perhaps communicate with a Phone (choose Bluetooth Low Energy!) but what if you want to send data very far? Most WiFi, Bluetooth, Zigbee and other wireless chipsets use 2.4GHz, which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
  NodeMCU V2.0: ESP8266 based NodeMCU
